// Logisim project control.circ as structural Verilog: 1 circuit, main circuit main
module main (
  input  Rep_31,
  input  LSB_Multiplier_1,
  input  Rep_32,
  input  LSB_Multiplier_0,
  input  CLK,
  output L_Product_MSB_Result,
  output L_Product_LSB_Result,
  output S_Product_msb,
  output S_Product_lsb,
  output L_Product_MSB,
  output L_Product_LSB,
  output L_carryout,
  output L_counter,
  output L_Reset
);

  wire and_1_out, and_2_out, and_3_out, and_4_out, and_5_out, N2_out, not_1_out, not_2_out, not_3_out,
       not_4_out, not_5_out, not_6_out, not_7_out, not_8_out, not_9_out, not_10_out, not_11_out, not_12_out,
       not_13_out, not_14_out, not_15_out, not_16_out, not_17_out, not_18_out, not_19_out, not_20_out,
       not_21_out, or_1_out, S0_2_out, S0_out;
  wire [2:0] N0_out, register_1_q;

  or or_1 (or_1_out, LSB_Multiplier_1, LSB_Multiplier_0);
  not not_1 (not_1_out, register_1_q[1]);
  not not_2 (not_2_out, register_1_q[0]);
  and S0 (S0_out, register_1_q[2], not_1_out, not_2_out);
  Register #(.width(3)) register_1 (.D(N0_out), .en(1'b1), .Q(register_1_q), .clk(CLK));  // open: clr
  not not_3 (not_3_out, register_1_q[2]);
  not not_4 (not_4_out, register_1_q[2]);
  not not_5 (not_5_out, register_1_q[0]);
  not not_6 (not_6_out, register_1_q[2]);
  not not_7 (not_7_out, register_1_q[1]);
  not not_8 (not_8_out, register_1_q[2]);
  not not_9 (not_9_out, register_1_q[1]);
  not not_10 (not_10_out, register_1_q[2]);
  not not_11 (not_11_out, register_1_q[2]);
  not not_12 (not_12_out, register_1_q[2]);
  not not_13 (not_13_out, register_1_q[0]);
  not not_14 (not_14_out, register_1_q[2]);
  not not_15 (not_15_out, register_1_q[1]);
  not not_16 (not_16_out, register_1_q[2]);
  not not_17 (not_17_out, register_1_q[1]);
  not not_18 (not_18_out, register_1_q[0]);
  and N2 (N2_out, not_3_out, register_1_q[1], Rep_31, register_1_q[0]);
  and and_1 (and_1_out, not_4_out, register_1_q[1], not_5_out);
  and and_2 (and_2_out, not_6_out, not_7_out, register_1_q[0], or_1_out);
  // AND_Gate S1 has open pins: in0=not_8_out, in1=not_9_out, in2=register_1_q[0], out=open
  and S3 (L_counter, not_10_out, register_1_q[1], register_1_q[0]);
  and and_3 (and_3_out, not_11_out, register_1_q[1], register_1_q[0], Rep_32);
  and S2 (L_carryout, not_12_out, register_1_q[1], not_13_out);
  and and_4 (and_4_out, not_14_out, not_15_out, register_1_q[0], LSB_Multiplier_0);
  and S0_2 (S0_2_out, not_16_out, not_17_out, not_18_out);
  or N2_2 (N0_out[2], N2_out, S0_out, and_5_out);
  not not_19 (not_19_out, register_1_q[1]);
  or N1 (N0_out[1], and_1_out, and_2_out);
  and and_5 (and_5_out, register_1_q[2], not_19_out, register_1_q[0]);
  not not_20 (not_20_out, register_1_q[1]);
  not not_21 (not_21_out, register_1_q[0]);
  or N0 (N0_out[0], and_5_out, and_3_out, L_carryout, S0_out, and_4_out, S0_2_out);
  and and_6 (L_Product_LSB_Result, register_1_q[2], not_20_out, not_21_out);
  or or_2 (L_Product_MSB, L_carryout, L_counter);
  or or_3 (L_Product_LSB, S0_2_out, L_counter);

  assign L_Product_MSB_Result = L_Product_LSB_Result;
  assign L_Reset = L_counter;
  assign S_Product_lsb = L_counter;
  assign S_Product_msb = L_counter;
endmodule
