// Logisim project datapath.circ as structural Verilog: 4 circuits, main circuit main
module main (
  input  S_Product_LSB,
  input  L_Product_Lsb_Result,
  input  [31:0] MULTIPLIER,
  input  L_Product_Lsb,
  input  L_CarryOut,
  input  L_Product_Msb_Result,
  input  Reset_CarryOut,
  input  S_Product_MSB,
  input  L_counter,
  input  L_Product_Msb,
  input  [31:0] MULTIPLICAND,
  input  CLK,
  output [31:0] PRDUCT_RIGHT_HALF,
  output Lsb_multiplier_0,
  output Lsbm_multiplier_1,
  output [31:0] PRDUCT_LEFT_HALF,
  output Rep___32,
  output Rep___31
);

  wire ADDER_cout, Carry_Out_q;
  wire [4:0] Counter_q;
  wire [31:0] ADDER_sum_output, multiplexer_1_out, multiplexer_2_out, PRODUCT_LSB_q, PRODUCT_MSB_q,
       shifter_1_product_lsb_output, shifter_1_product_msb_output;

  Register #(.width(1)) Carry_Out (.D(ADDER_cout), .en(L_CarryOut), .Q(Carry_Out_q), .clk(CLK), .clr(Reset_CarryOut));
  shifter shifter_1 (
    .PRODUCT_MSB_Input(PRODUCT_MSB_q), .Cin(Carry_Out_q), .PRODUCT_LSB_Input(PRODUCT_LSB_q),
    .PRODUCT_MSB_Output(shifter_1_product_msb_output), .PRODUCT_LSB_Output(shifter_1_product_lsb_output));
  _32bit_Adder ADDER (
    .A_input(MULTIPLICAND), .B_input(PRODUCT_MSB_q), .SUM_OUTPUT(ADDER_sum_output), .COUT(ADDER_cout));
  Multiplexer #(.width(32), .enable("false")) multiplexer_1 (
    .in0(MULTIPLIER), .in1(shifter_1_product_lsb_output), .out(multiplexer_1_out), .sel(S_Product_LSB));
  Multiplexer #(.width(32), .enable("false")) multiplexer_2 (
    .in0(ADDER_sum_output), .in1(shifter_1_product_msb_output), .out(multiplexer_2_out), .sel(S_Product_MSB));
  Register #(.width(32)) PRODUCT_LSB (
    .D(multiplexer_1_out), .en(L_Product_Lsb), .Q(PRODUCT_LSB_q), .clk(CLK));  // open: clr
  Register #(.width(32)) PRODUCT_MSB (
    .D(multiplexer_2_out), .en(L_Product_Msb), .Q(PRODUCT_MSB_q), .clk(CLK));  // open: clr
  Register #(.width(32)) PRODUCT_LSB_2 (
    .D(PRODUCT_LSB_q), .en(L_Product_Lsb_Result), .Q(PRDUCT_RIGHT_HALF), .clk(CLK));  // open: clr
  Comparator #(.width(1), .mode("unsigned")) comparator_1 (
    .a(1'b1), .b(PRODUCT_LSB_q[0]), .gt(Lsb_multiplier_0), .eq(Lsbm_multiplier_1));  // open: lt
  Register #(.width(32)) PRODUCT_MSB_2 (
    .D(PRODUCT_MSB_q), .en(L_Product_Msb_Result), .Q(PRDUCT_LEFT_HALF), .clk(CLK));  // open: clr
  Counter #(.width(5), .max('h1f)) Counter (.count(L_counter), .Q(Counter_q), .clk(CLK));  // open: load, D, carry, clr
  Comparator #(.width(5), .mode("unsigned")) comparator_2 (
    .a({5{1'b1}}), .b(Counter_q), .gt(Rep___32), .eq(Rep___31));  // open: lt

  // Notes on the sheet:
  //   Shifter
endmodule

module shifter (
  input  [31:0] PRODUCT_MSB_Input,
  input  Cin,
  input  [31:0] PRODUCT_LSB_Input,
  output [31:0] PRODUCT_MSB_Output,
  output [31:0] PRODUCT_LSB_Output
);


  assign PRODUCT_LSB_Output = {PRODUCT_MSB_Input[0], PRODUCT_LSB_Input[31:1]};
  assign PRODUCT_MSB_Output = {Cin, PRODUCT_MSB_Input[31:1]};
endmodule

module adder (
  input  Ci,
  input  Ai,
  input  Bi,
  output Sout,
  output Cout
);

  wire and_1_out, and_2_out, and_3_out, not_1_out, not_2_out, or_1_out, or_2_out;

  or or_1 (or_1_out, Ai, Bi);
  and and_1 (and_1_out, Bi, Ai);
  not not_1 (not_1_out, and_1_out);
  and and_2 (and_2_out, or_1_out, not_1_out);
  or or_2 (or_2_out, Ci, and_2_out);
  and and_3 (and_3_out, Ci, and_2_out);
  not not_2 (not_2_out, and_3_out);
  or or_3 (Cout, and_3_out, and_1_out);
  and and_4 (Sout, or_2_out, not_2_out);
endmodule

module _32bit_Adder (
  input  [31:0] A_input,
  input  [31:0] B_input,
  output [31:0] SUM_OUTPUT,
  output COUT
);

  wire adder_1_cout, adder_2_cout, adder_3_cout, adder_4_cout, adder_5_cout, adder_6_cout, adder_7_cout,
       adder_8_cout, adder_9_cout, adder_10_cout, adder_11_cout, adder_12_cout, adder_13_cout, adder_14_cout,
       adder_15_cout, adder_16_cout, adder_17_cout, adder_18_cout, adder_19_cout, adder_20_cout,
       adder_21_cout, adder_22_cout, adder_23_cout, adder_24_cout, adder_25_cout, adder_26_cout,
       adder_27_cout, adder_28_cout, adder_29_cout, adder_30_cout, adder_31_cout;

  adder adder_1 (.Ai(A_input[0]), .Bi(B_input[0]), .Ci(1'b0), .Sout(SUM_OUTPUT[0]), .Cout(adder_1_cout));
  adder adder_2 (.Ai(A_input[1]), .Bi(B_input[1]), .Ci(adder_1_cout), .Sout(SUM_OUTPUT[1]), .Cout(adder_2_cout));
  adder adder_3 (.Ai(A_input[2]), .Bi(B_input[2]), .Ci(adder_2_cout), .Sout(SUM_OUTPUT[2]), .Cout(adder_3_cout));
  adder adder_4 (.Ai(A_input[3]), .Bi(B_input[3]), .Ci(adder_3_cout), .Sout(SUM_OUTPUT[3]), .Cout(adder_4_cout));
  adder adder_5 (.Ai(A_input[4]), .Bi(B_input[4]), .Ci(adder_4_cout), .Sout(SUM_OUTPUT[4]), .Cout(adder_5_cout));
  adder adder_6 (.Ai(A_input[5]), .Bi(B_input[5]), .Ci(adder_5_cout), .Sout(SUM_OUTPUT[5]), .Cout(adder_6_cout));
  adder adder_7 (.Ai(A_input[6]), .Bi(B_input[6]), .Ci(adder_6_cout), .Sout(SUM_OUTPUT[6]), .Cout(adder_7_cout));
  adder adder_8 (.Ai(A_input[7]), .Bi(B_input[7]), .Ci(adder_7_cout), .Sout(SUM_OUTPUT[7]), .Cout(adder_8_cout));
  adder adder_9 (.Ai(A_input[8]), .Bi(B_input[8]), .Ci(adder_8_cout), .Sout(SUM_OUTPUT[8]), .Cout(adder_9_cout));
  adder adder_10 (.Ai(A_input[9]), .Bi(B_input[9]), .Ci(adder_9_cout), .Sout(SUM_OUTPUT[9]), .Cout(adder_10_cout));
  adder adder_11 (.Ai(A_input[10]), .Bi(B_input[10]), .Ci(adder_10_cout), .Sout(SUM_OUTPUT[10]), .Cout(adder_11_cout));
  adder adder_12 (.Ai(A_input[11]), .Bi(B_input[11]), .Ci(adder_11_cout), .Sout(SUM_OUTPUT[11]), .Cout(adder_12_cout));
  adder adder_13 (.Ai(A_input[12]), .Bi(B_input[12]), .Ci(adder_12_cout), .Sout(SUM_OUTPUT[12]), .Cout(adder_13_cout));
  adder adder_14 (.Ai(A_input[13]), .Bi(B_input[13]), .Ci(adder_13_cout), .Sout(SUM_OUTPUT[13]), .Cout(adder_14_cout));
  adder adder_15 (.Ai(A_input[14]), .Bi(B_input[14]), .Ci(adder_14_cout), .Sout(SUM_OUTPUT[14]), .Cout(adder_15_cout));
  adder adder_16 (.Ai(A_input[15]), .Bi(B_input[15]), .Ci(adder_15_cout), .Sout(SUM_OUTPUT[15]), .Cout(adder_16_cout));
  adder adder_17 (.Ai(A_input[16]), .Bi(B_input[16]), .Ci(adder_16_cout), .Sout(SUM_OUTPUT[16]), .Cout(adder_17_cout));
  adder adder_18 (.Ai(A_input[17]), .Bi(B_input[17]), .Ci(adder_17_cout), .Sout(SUM_OUTPUT[17]), .Cout(adder_18_cout));
  adder adder_19 (.Ai(A_input[18]), .Bi(B_input[18]), .Ci(adder_18_cout), .Sout(SUM_OUTPUT[18]), .Cout(adder_19_cout));
  adder adder_20 (.Ai(A_input[19]), .Bi(B_input[19]), .Ci(adder_19_cout), .Sout(SUM_OUTPUT[19]), .Cout(adder_20_cout));
  adder adder_21 (.Ai(A_input[20]), .Bi(B_input[20]), .Ci(adder_20_cout), .Sout(SUM_OUTPUT[20]), .Cout(adder_21_cout));
  adder adder_22 (.Ai(A_input[21]), .Bi(B_input[21]), .Ci(adder_21_cout), .Sout(SUM_OUTPUT[21]), .Cout(adder_22_cout));
  adder adder_23 (.Ai(A_input[22]), .Bi(B_input[22]), .Ci(adder_22_cout), .Sout(SUM_OUTPUT[22]), .Cout(adder_23_cout));
  adder adder_24 (.Ai(A_input[23]), .Bi(B_input[23]), .Ci(adder_23_cout), .Sout(SUM_OUTPUT[23]), .Cout(adder_24_cout));
  adder adder_25 (.Ai(A_input[24]), .Bi(B_input[24]), .Ci(adder_24_cout), .Sout(SUM_OUTPUT[24]), .Cout(adder_25_cout));
  adder adder_26 (.Ai(A_input[25]), .Bi(B_input[25]), .Ci(adder_25_cout), .Sout(SUM_OUTPUT[25]), .Cout(adder_26_cout));
  adder adder_27 (.Ai(A_input[26]), .Bi(B_input[26]), .Ci(adder_26_cout), .Sout(SUM_OUTPUT[26]), .Cout(adder_27_cout));
  adder adder_28 (.Ai(A_input[27]), .Bi(B_input[27]), .Ci(adder_27_cout), .Sout(SUM_OUTPUT[27]), .Cout(adder_28_cout));
  adder adder_29 (.Ai(A_input[28]), .Bi(B_input[28]), .Ci(adder_28_cout), .Sout(SUM_OUTPUT[28]), .Cout(adder_29_cout));
  adder adder_30 (.Ai(A_input[29]), .Bi(B_input[29]), .Ci(adder_29_cout), .Sout(SUM_OUTPUT[29]), .Cout(adder_30_cout));
  adder adder_31 (.Ai(A_input[30]), .Bi(B_input[30]), .Ci(adder_30_cout), .Sout(SUM_OUTPUT[30]), .Cout(adder_31_cout));
  adder adder_32 (.Ai(A_input[31]), .Bi(B_input[31]), .Ci(adder_31_cout), .Sout(SUM_OUTPUT[31]), .Cout(COUT));

  // Notes on the sheet:
  //   LSB
  //   MSB
endmodule
