// Logisim project mult32.circ as structural Verilog: 1 circuit, main circuit main
module main (
  input  [31:0] in_1,
  input  [31:0] in_2,
  output [31:0] out_3,
  output [31:0] out_4
);

  wire clock_1_out, main_1_lsb_multiplier_0, main_1_lsbm_multiplier_1, main_1_rep___31, main_1_rep___32,
       main_2_l_carryout, main_2_l_counter, main_2_l_product_lsb, main_2_l_product_lsb_result,
       main_2_l_product_msb, main_2_l_product_msb_result, main_2_l_reset, main_2_s_product_lsb,
       main_2_s_product_msb;

  datapath_main main_1 (
    .S_Product_LSB(main_2_s_product_lsb), .L_Product_Lsb_Result(main_2_l_product_lsb_result),
    .MULTIPLIER(in_1), .L_Product_Lsb(main_2_l_product_lsb), .L_CarryOut(main_2_l_carryout),
    .L_Product_Msb_Result(main_2_l_product_msb_result), .Reset_CarryOut(main_2_l_reset),
    .S_Product_MSB(main_2_s_product_msb), .L_counter(main_2_l_counter), .L_Product_Msb(main_2_l_product_msb),
    .MULTIPLICAND(in_2), .CLK(clock_1_out), .PRDUCT_RIGHT_HALF(out_4),
    .Lsb_multiplier_0(main_1_lsb_multiplier_0), .Lsbm_multiplier_1(main_1_lsbm_multiplier_1),
    .PRDUCT_LEFT_HALF(out_3), .Rep___32(main_1_rep___32), .Rep___31(main_1_rep___31));
  Clock clock_1 (.out(clock_1_out));
  control_main main_2 (
    .Rep_31(main_1_rep___31), .LSB_Multiplier_1(main_1_lsbm_multiplier_1), .Rep_32(main_1_rep___32),
    .LSB_Multiplier_0(main_1_lsb_multiplier_0), .CLK(clock_1_out),
    .L_Product_MSB_Result(main_2_l_product_msb_result), .L_Product_LSB_Result(main_2_l_product_lsb_result),
    .S_Product_msb(main_2_s_product_msb), .S_Product_lsb(main_2_s_product_lsb),
    .L_Product_MSB(main_2_l_product_msb), .L_Product_LSB(main_2_l_product_lsb),
    .L_carryout(main_2_l_carryout), .L_counter(main_2_l_counter), .L_Reset(main_2_l_reset));

  // Notes on the sheet:
  //   Multiplier
  //   x
  //   Multiplicand
  //   =
  //   Product
endmodule
